// Logisim project address_decoding.circ as structural Verilog: 3 circuits, main circuit main
module main (
  input  in_1,
  input  in_2,
  input  in_3,
  input  in_4,
  input  in_5,
  input  in_6,
  input  in_7,
  input  in_8,
  input  in_9,
  input  in_10,
  input  in_11,
  input  in_12,
  input  in_13,
  input  in_14,
  input  in_15,
  input  in_16,
  input  in_17,
  input  in_18,
  input  in_19,
  input  in_20,
  input  in_21,
  input  in_22,
  input  in_23,
  input  in_24,
  input  in_25
);

  wire AY, AY_BC1, AY_BDIR, AYSELb, C1W, C1WSELb, C2W, C2WSELb, CR, CRSELb, CRT8, CRT8SELb, CRTA, CRTASELb,
       CRTC, CRTCSELb, CRTE, CRTESELb, FF1W, FF1WSELb, FF2W, FF2WSELb, M1WAIT, not_1_out, not_2_out,
       or_1_out, or_2_out, R10, R11, R12, RAMSELb, ROMSELb, SNW, SNWSELb, VDPEN, VDPR, VDPRSELb, VDPW,
       VDPWSELb;
  wire [3:0] controlled_buffer_2_out, controlled_buffer_9_out, controlled_buffer_10_out,
       controlled_buffer_16_out, controlled_buffer_17_out, controlled_buffer_23_out,
       controlled_buffer_25_out, controlled_buffer_31_out, controlled_buffer_37_out,
       controlled_buffer_38_out, controlled_buffer_45_out, controlled_buffer_46_out,
       controlled_buffer_51_out, controlled_buffer_53_out;

  assign controlled_buffer_2_out[3] = not_1_out ? 1'b0 : 1'bz;  // Controlled_Buffer controlled_buffer_1
  not not_1 (not_1_out, RAMSELb);
  assign controlled_buffer_2_out[0] = not_1_out ? R12 : 1'bz;  // Controlled_Buffer controlled_buffer_2
  assign controlled_buffer_2_out[1] = not_1_out ? in_6 : 1'bz;  // Controlled_Buffer controlled_buffer_3
  assign controlled_buffer_2_out[2] = not_1_out ? in_5 : 1'bz;  // Controlled_Buffer controlled_buffer_4
  assign controlled_buffer_9_out[1] = not_1_out ? in_10 : 1'bz;  // Controlled_Buffer controlled_buffer_5
  assign controlled_buffer_9_out[2] = not_1_out ? R10 : 1'bz;  // Controlled_Buffer controlled_buffer_6
  assign controlled_buffer_9_out[3] = not_1_out ? R11 : 1'bz;  // Controlled_Buffer controlled_buffer_7
  assign controlled_buffer_10_out[3] = not_1_out ? in_12 : 1'bz;  // Controlled_Buffer controlled_buffer_8
  Hex_Digit_Display hex_digit_display_1 (.value(controlled_buffer_2_out));  // open: dp
  assign controlled_buffer_9_out[0] = not_1_out ? in_11 : 1'bz;  // Controlled_Buffer controlled_buffer_9
  assign controlled_buffer_10_out[0] = not_1_out ? in_15 : 1'bz;  // Controlled_Buffer controlled_buffer_10
  assign controlled_buffer_10_out[1] = not_1_out ? in_14 : 1'bz;  // Controlled_Buffer controlled_buffer_11
  assign controlled_buffer_10_out[2] = not_1_out ? in_13 : 1'bz;  // Controlled_Buffer controlled_buffer_12
  assign controlled_buffer_16_out[1] = not_1_out ? in_18 : 1'bz;  // Controlled_Buffer controlled_buffer_13
  assign controlled_buffer_16_out[2] = not_1_out ? in_17 : 1'bz;  // Controlled_Buffer controlled_buffer_14
  assign controlled_buffer_16_out[3] = not_1_out ? in_16 : 1'bz;  // Controlled_Buffer controlled_buffer_15
  Hex_Digit_Display hex_digit_display_2 (.value(controlled_buffer_9_out));  // open: dp
  Hex_Digit_Display hex_digit_display_3 (.value(controlled_buffer_10_out));  // open: dp
  assign controlled_buffer_16_out[0] = not_1_out ? in_19 : 1'bz;  // Controlled_Buffer controlled_buffer_16
  assign controlled_buffer_17_out[0] = not_2_out ? in_7 : 1'bz;  // Controlled_Buffer controlled_buffer_17
  assign controlled_buffer_17_out[1] = not_2_out ? 1'b0 : 1'bz;  // Controlled_Buffer controlled_buffer_18
  assign controlled_buffer_17_out[2] = not_2_out ? 1'b0 : 1'bz;  // Controlled_Buffer controlled_buffer_19
  assign controlled_buffer_17_out[3] = not_2_out ? 1'b0 : 1'bz;  // Controlled_Buffer controlled_buffer_20
  assign controlled_buffer_23_out[2] = not_2_out ? in_9 : 1'bz;  // Controlled_Buffer controlled_buffer_21
  assign controlled_buffer_23_out[3] = not_2_out ? in_8 : 1'bz;  // Controlled_Buffer controlled_buffer_22
  not not_2 (not_2_out, ROMSELb);
  IODEC iodec_1 (
    .IORQb(in_21), .WRb(in_22), .A0(in_19), .A1(in_18), .A2(in_17), .A3(in_16), .A4(in_15), .A5(in_14),
    .A6(in_13), .A7(in_12), .C2WSELb(C2WSELb), .VDPRSELb(VDPRSELb), .VDPWSELb(VDPWSELb), .VDPEN(VDPEN),
    .C1WSELb(C1WSELb), .CRSELb(CRSELb), .SNWSELb(SNWSELb), .AYSELb(AYSELb), .FF1WSELb(FF1WSELb),
    .FF2WSELb(FF2WSELb));
  MEMDEC memdec_1 (
    .MREQb(in_20), .RDb(in_23), .RFSHb(in_1), .CLK(in_2), .M1(in_3), .XRAMEN(in_24), .ROMEN(in_25),
    .A13(in_6), .A14(in_5), .A15(in_4), .RAMSELb(RAMSELb), .ROMSELb(ROMSELb), .CRT8SELb(CRT8SELb),
    .CRTASELb(CRTASELb), .CRTCSELb(CRTCSELb), .CRTESELb(CRTESELb), .M1WAIT(M1WAIT));
  Hex_Digit_Display hex_digit_display_4 (.value(controlled_buffer_16_out));  // open: dp
  Hex_Digit_Display hex_digit_display_5 (.value(controlled_buffer_17_out));  // open: dp
  assign controlled_buffer_23_out[0] = not_2_out ? in_11 : 1'bz;  // Controlled_Buffer controlled_buffer_23
  assign controlled_buffer_23_out[1] = not_2_out ? in_10 : 1'bz;  // Controlled_Buffer controlled_buffer_24
  assign controlled_buffer_25_out[0] = not_2_out ? in_15 : 1'bz;  // Controlled_Buffer controlled_buffer_25
  assign controlled_buffer_25_out[1] = not_2_out ? in_14 : 1'bz;  // Controlled_Buffer controlled_buffer_26
  assign controlled_buffer_25_out[2] = not_2_out ? in_13 : 1'bz;  // Controlled_Buffer controlled_buffer_27
  assign controlled_buffer_25_out[3] = not_2_out ? in_12 : 1'bz;  // Controlled_Buffer controlled_buffer_28
  assign controlled_buffer_31_out[2] = not_2_out ? in_17 : 1'bz;  // Controlled_Buffer controlled_buffer_29
  assign controlled_buffer_31_out[3] = not_2_out ? in_16 : 1'bz;  // Controlled_Buffer controlled_buffer_30
  not not_3 (C2W, C2WSELb);
  not not_4 (VDPR, VDPRSELb);
  not not_5 (VDPW, VDPWSELb);
  not not_6 (C1W, C1WSELb);
  not not_7 (CR, CRSELb);
  not not_8 (SNW, SNWSELb);
  not not_9 (AY, AYSELb);
  not not_10 (FF1W, FF1WSELb);
  not not_11 (FF2W, FF2WSELb);
  Hex_Digit_Display hex_digit_display_6 (.value(controlled_buffer_23_out));  // open: dp
  Hex_Digit_Display hex_digit_display_7 (.value(controlled_buffer_25_out));  // open: dp
  assign controlled_buffer_31_out[0] = not_2_out ? in_19 : 1'bz;  // Controlled_Buffer controlled_buffer_31
  assign controlled_buffer_31_out[1] = not_2_out ? in_18 : 1'bz;  // Controlled_Buffer controlled_buffer_32
  assign controlled_buffer_37_out[1] = or_1_out ? in_6 : 1'bz;  // Controlled_Buffer controlled_buffer_33
  assign controlled_buffer_37_out[2] = or_1_out ? in_5 : 1'bz;  // Controlled_Buffer controlled_buffer_34
  assign controlled_buffer_37_out[3] = or_1_out ? 1'b0 : 1'bz;  // Controlled_Buffer controlled_buffer_35
  assign controlled_buffer_38_out[3] = or_1_out ? in_8 : 1'bz;  // Controlled_Buffer controlled_buffer_36
  or or_1 (or_1_out, CRT8, CRTA, CRTC, CRTE);
  Hex_Digit_Display hex_digit_display_8 (.value(controlled_buffer_31_out));  // open: dp
  assign controlled_buffer_37_out[0] = or_1_out ? in_7 : 1'bz;  // Controlled_Buffer controlled_buffer_37
  assign controlled_buffer_38_out[0] = or_1_out ? in_11 : 1'bz;  // Controlled_Buffer controlled_buffer_38
  assign controlled_buffer_38_out[1] = or_1_out ? in_10 : 1'bz;  // Controlled_Buffer controlled_buffer_39
  assign controlled_buffer_38_out[2] = or_1_out ? in_9 : 1'bz;  // Controlled_Buffer controlled_buffer_40
  assign controlled_buffer_45_out[1] = or_1_out ? in_14 : 1'bz;  // Controlled_Buffer controlled_buffer_41
  assign controlled_buffer_45_out[2] = or_1_out ? in_13 : 1'bz;  // Controlled_Buffer controlled_buffer_42
  assign controlled_buffer_45_out[3] = or_1_out ? in_12 : 1'bz;  // Controlled_Buffer controlled_buffer_43
  assign controlled_buffer_46_out[3] = or_1_out ? in_16 : 1'bz;  // Controlled_Buffer controlled_buffer_44
  LED led_1 (.in(CRT8));
  LED led_2 (.in(CRTC));
  Hex_Digit_Display hex_digit_display_9 (.value(controlled_buffer_37_out));  // open: dp
  Hex_Digit_Display hex_digit_display_10 (.value(controlled_buffer_38_out));  // open: dp
  assign controlled_buffer_45_out[0] = or_1_out ? in_15 : 1'bz;  // Controlled_Buffer controlled_buffer_45
  assign controlled_buffer_46_out[0] = or_1_out ? in_19 : 1'bz;  // Controlled_Buffer controlled_buffer_46
  assign controlled_buffer_46_out[1] = or_1_out ? in_18 : 1'bz;  // Controlled_Buffer controlled_buffer_47
  assign controlled_buffer_46_out[2] = or_1_out ? in_17 : 1'bz;  // Controlled_Buffer controlled_buffer_48
  assign controlled_buffer_51_out[2] = or_2_out ? in_13 : 1'bz;  // Controlled_Buffer controlled_buffer_49
  assign controlled_buffer_51_out[3] = or_2_out ? in_12 : 1'bz;  // Controlled_Buffer controlled_buffer_50
  or or_2 (or_2_out, C2W, VDPR, VDPW, C1W, CR, SNW, AY, FF1W, FF2W);
  and and_1 (R10, in_9, in_24);
  and and_2 (R11, in_8, in_24);
  and and_3 (R12, in_7, in_24);
  LED led_3 (.in(CRTA));
  LED led_4 (.in(CRTE));
  Hex_Digit_Display hex_digit_display_11 (.value(controlled_buffer_45_out));  // open: dp
  Hex_Digit_Display hex_digit_display_12 (.value(controlled_buffer_46_out));  // open: dp
  not not_12 (CRT8, CRT8SELb);
  not not_13 (CRTA, CRTASELb);
  not not_14 (CRTC, CRTCSELb);
  not not_15 (CRTE, CRTESELb);
  assign controlled_buffer_51_out[0] = or_2_out ? in_15 : 1'bz;  // Controlled_Buffer controlled_buffer_51
  assign controlled_buffer_51_out[1] = or_2_out ? in_14 : 1'bz;  // Controlled_Buffer controlled_buffer_52
  assign controlled_buffer_53_out[0] = or_2_out ? in_19 : 1'bz;  // Controlled_Buffer controlled_buffer_53
  assign controlled_buffer_53_out[1] = or_2_out ? in_18 : 1'bz;  // Controlled_Buffer controlled_buffer_54
  assign controlled_buffer_53_out[2] = or_2_out ? in_17 : 1'bz;  // Controlled_Buffer controlled_buffer_55
  assign controlled_buffer_53_out[3] = or_2_out ? in_16 : 1'bz;  // Controlled_Buffer controlled_buffer_56
  LED led_5 (.in(C1W));
  LED led_6 (.in(SNW));
  LED led_7 (.in(VDPR));
  Hex_Digit_Display hex_digit_display_13 (.value(controlled_buffer_51_out));  // open: dp
  Hex_Digit_Display hex_digit_display_14 (.value(controlled_buffer_53_out));  // open: dp
  LED led_8 (.in(C2W));
  LED led_9 (.in(CR));
  LED led_10 (.in(AY));
  LED led_11 (.in(AY_BC1));
  LED led_12 (.in(VDPW));
  LED led_13 (.in(VDPEN));
  LED led_14 (.in(FF1W));
  nor nor_1 (AY_BC1, in_19, AYSELb);
  nor nor_2 (AY_BDIR, AYSELb, in_22);
  LED led_15 (.in(AY_BDIR));
  LED led_16 (.in(FF2W));

  // Other names for the same wires on the sheet: A0 = in_19; A1 = in_18; A2 = in_17; A3 = in_16; A4 = in_15;
  //   A5 = in_14; A6 = in_13; A7 = in_12; A8 = in_11; A9 = in_10; A10 = in_9; A11 = in_8; A12 = in_7; A13 = in_6;
  //   A14 = in_5; A15 = in_4; IORQb = in_21; MREQb = in_20; RDb = in_23; ROMEN = in_25; WRb = in_22; XRAMEN = in_24

  // Notes on the sheet:
  //   RAM address
  //   ROM address
  //   CART address
  //   I/O address
endmodule

module IODEC (
  input  IORQb,
  input  WRb,
  input  A0,
  input  A1,
  input  A2,
  input  A3,
  input  A4,
  input  A5,
  input  A6,
  input  A7,
  output C2WSELb,
  output VDPRSELb,
  output VDPWSELb,
  output VDPEN,
  output C1WSELb,
  output CRSELb,
  output SNWSELb,
  output AYSELb,
  output FF1WSELb,
  output FF2WSELb
);

  wire and_8_out, and_9_out, and_10_out, AYSEL, C1WSEL, C2WSEL, CRSEL, FF1WSEL, FF2WSEL, IORQ, nA0, nA1, nA2,
       nA3, nA5, nA6, nA7, SNWSEL, VDPRSEL, VDPWSEL, WR;

  not not_1 (IORQ, IORQb);
  not not_2 (nA0, A0);
  not not_3 (nA2, A2);
  not not_4 (nA6, A6);
  and and_1 (C2WSEL, A7, nA6, nA5, IORQ, WR);
  and and_2 (VDPRSEL, A7, nA6, A5, IORQ, WRb);
  and and_3 (VDPWSEL, A7, nA6, A5, IORQ, WR);
  and and_4 (VDPEN, A7, nA6, A5, IORQ);
  and and_5 (C1WSEL, A7, A6, nA5, IORQ, WR);
  and and_6 (CRSEL, A7, A6, A5, IORQ, WRb);
  and and_7 (SNWSEL, A7, A6, A5, IORQ, WR);
  not not_5 (WR, WRb);
  not not_6 (nA1, A1);
  not not_7 (nA3, A3);
  not not_8 (nA5, A5);
  not not_9 (nA7, A7);
  not not_10 (C2WSELb, C2WSEL);
  LED led_1 (.in(C2WSELb));
  not not_11 (VDPWSELb, VDPWSEL);
  LED led_2 (.in(VDPWSELb));
  not not_12 (C1WSELb, C1WSEL);
  LED led_3 (.in(C1WSELb));
  not not_13 (SNWSELb, SNWSEL);
  LED led_4 (.in(SNWSELb));
  not not_14 (FF1WSELb, FF1WSEL);
  LED led_5 (.in(FF1WSELb));
  and and_8 (and_8_out, nA7, A6, nA5, A4, nA3, nA2, nA1, nA0, IORQ);
  and and_9 (and_9_out, nA7, A6, nA5, A4, nA3, nA2, nA1, A0, IORQ);
  and and_10 (and_10_out, nA7, A6, nA5, A4, nA3, nA2, A1, nA0, IORQ);
  or or_1 (AYSEL, and_8_out, and_9_out, and_10_out);
  not not_15 (VDPRSELb, VDPRSEL);
  LED led_6 (.in(VDPRSELb));
  LED led_7 (.in(VDPEN));
  not not_16 (CRSELb, CRSEL);
  LED led_8 (.in(CRSELb));
  not not_17 (AYSELb, AYSEL);
  LED led_9 (.in(AYSELb));
  not not_18 (FF2WSELb, FF2WSEL);
  LED led_10 (.in(FF2WSELb));
  and and_11 (FF1WSEL, nA7, A6, nA5, A4, nA3, nA2, A1, A0, IORQ, WR);
  and and_12 (FF2WSEL, nA7, A6, A5, A4, A3, A2, A1, A0, IORQ, WR);

  // Other names for the same wires on the sheet: nWR = WRb

  // Notes on the sheet:
  //   $8x (w)
  //   $Ax (r)
  //   $Ax (w)
  //   $Ax
  //   $Cx (w)
  //   $Ex (r)
  //   $Ex (w)
  //   $50
  //   $51
  //   $52
  //   $53 (w)
  //   $7F (w)
endmodule

module MEMDEC (
  input  MREQb,
  input  RDb,
  input  RFSHb,
  input  CLK,
  input  M1,
  input  XRAMEN,
  input  ROMEN,
  input  A13,
  input  A14,
  input  A15,
  output RAMSELb,
  output ROMSELb,
  output CRT8SELb,
  output CRTASELb,
  output CRTCSELb,
  output CRTESELb,
  output M1WAIT
);

  wire and_2_out, and_3_out, and_4_out, and_5_out, and_6_out, CRT8SEL, CRTASEL, CRTCSEL, CRTESEL, MREQ, nA13,
       nA14, nA15, not_14_out, nROMEN, RAMSEL, RD, RFSH, ROMSEL;

  not not_1 (MREQ, MREQb);
  not not_2 (RD, RDb);
  not not_3 (RFSH, RFSHb);
  not not_4 (nROMEN, ROMEN);
  not not_5 (nA13, A13);
  not not_6 (nA14, A14);
  not not_7 (nA15, A15);
  and and_1 (ROMSEL, nA13, nA14, nA15, MREQ, RFSHb, RD, ROMEN);
  and and_2 (and_2_out, nA13, nA14, nA15, MREQ, RFSHb, RD, nROMEN);
  and and_3 (and_3_out, nA13, nA14, nA15, MREQ, RFSHb, RDb);
  and and_4 (and_4_out, A13, nA14, nA15, MREQ, RFSHb, XRAMEN);
  and and_5 (and_5_out, nA13, A14, nA15, MREQ, RFSHb, XRAMEN);
  and and_6 (and_6_out, A13, A14, nA15, MREQ, RFSHb);
  or or_1 (RAMSEL, and_2_out, and_3_out, and_4_out, and_5_out, and_6_out);
  not not_8 (RAMSELb, RAMSEL);
  LED led_1 (.in(RAMSELb));
  not not_9 (ROMSELb, ROMSEL);
  LED led_2 (.in(ROMSELb));
  not not_10 (CRT8SELb, CRT8SEL);
  LED led_3 (.in(CRT8SELb));
  not not_11 (CRTASELb, CRTASEL);
  LED led_4 (.in(CRTASELb));
  not not_12 (CRTCSELb, CRTCSEL);
  LED led_5 (.in(CRTCSELb));
  not not_13 (CRTESELb, CRTESEL);
  LED led_6 (.in(CRTESELb));
  LED led_7 (.in(M1WAIT));
  not not_14 (not_14_out, M1WAIT);
  D_Flip_Flop d_ff_1 (.D(not_14_out), .clk(CLK), .Q(M1WAIT), .reset(M1));  // open: Qn, preset
  and and_7 (CRT8SEL, nA13, nA14, A15, MREQ, RFSHb);
  and and_8 (CRTASEL, A13, nA14, A15, MREQ, RFSHb);
  and and_9 (CRTCSEL, nA13, A14, A15, MREQ, RFSHb);
  and and_10 (CRTESEL, A13, A14, A15, MREQ, RFSHb);

  // Other names for the same wires on the sheet: nRD = RDb; nRFSH = RFSHb
endmodule
