// Logisim project ay_clock_fix_interposer.circ as structural Verilog: 1 circuit, main circuit main
module main (
  input  RESETb
);

  wire AYCLK, CPUCLK, d_ff_1_qn, not_1_out;

  Clock u_CPUCLK (.out(CPUCLK));
  // Digital_Oscilloscope #(.nState(16)) digital_oscilloscope_1: pin names not known; wires that end beside it: CPUCLK, AYCLK
  D_Flip_Flop d_ff_1 (.D(d_ff_1_qn), .clk(CPUCLK), .Q(AYCLK), .Qn(d_ff_1_qn), .preset(1'b0), .reset(not_1_out));
  not not_1 (not_1_out, RESETb);
endmodule
